# Fritzing sketch bfc3000_wemos (saved by Fritzing 0.9.2b)

parts:
  WeMos_D1_Mini1 = WeMos D1 Mini
  WeMos_D1_Mini_Protoboard_Shield1 = WeMos D1 Mini Protoboard Shield
  WeMos_D1_Mini_Battery_Shield1 = WeMos D1 Mini Battery Shield
  PIR1 = PIR sensor

nets:
  5V: WeMos_D1_Mini1.5V, WeMos_D1_Mini_Protoboard_Shield1.5V, WeMos_D1_Mini_Protoboard_Shield1.X7-Y8, WeMos_D1_Mini_Battery_Shield1.5V, PIR1.VDD
  N1: WeMos_D1_Mini1.G, WeMos_D1_Mini_Protoboard_Shield1.G, WeMos_D1_Mini_Protoboard_Shield1.X7-Y7, WeMos_D1_Mini_Battery_Shield1.G, PIR1.GND
  N2: WeMos_D1_Mini1.RST, WeMos_D1_Mini_Protoboard_Shield1.RST, WeMos_D1_Mini_Protoboard_Shield1.X2-Y1, PIR1.SIG

notes:
  battery shield's
  power connector to solar lamp circuit
